// Logisim project zaahler_fertig.circ as structural Verilog: 1 circuit, main circuit main
module main (
  input  in_1
);

  wire clock_1_out, nand_1_out, nand_2_out, nand_3_out, nand_4_out, nand_5_out, nand_6_out, nand_7_out,
       nand_8_out, nand_9_out, nand_10_out, nand_11_out, not_1_out, not_2_out, not_3_out, not_4_out;
  wire [3:0] counter_1_q;

  Clock clock_1 (.out(clock_1_out));
  Counter #(.max('hf), .width(4)) counter_1 (
    .clr(nand_11_out), .up(in_1), .count(in_1), .clk(clock_1_out), .Q(counter_1_q));  // open: load, D, carry
  nand nand_1 (nand_1_out, counter_1_q[0], counter_1_q[2]);
  nand nand_2 (nand_2_out, counter_1_q[0], counter_1_q[0]);
  nand nand_3 (nand_3_out, counter_1_q[2], counter_1_q[2]);
  nand nand_4 (nand_4_out, counter_1_q[2], counter_1_q[2]);
  nand nand_5 (nand_5_out, counter_1_q[1], counter_1_q[1]);
  nand nand_6 (nand_6_out, nand_2_out, nand_3_out);
  nand nand_7 (nand_7_out, nand_4_out, nand_5_out);
  nand nand_8 (nand_8_out, nand_6_out, nand_6_out);
  nand nand_9 (nand_9_out, nand_7_out, nand_7_out);
  LED led_1 (.in(counter_1_q[0]));
  LED led_2 (.in(counter_1_q[1]));
  LED led_3 (.in(counter_1_q[2]));
  LED led_4 (.in(counter_1_q[3]));
  nand nand_10 (nand_10_out, counter_1_q[1], counter_1_q[2]);
  nand nand_11 (nand_11_out, nand_10_out, nand_10_out);
  not not_1 (not_1_out, nand_1_out);
  not not_2 (not_2_out, nand_8_out);
  not not_3 (not_3_out, nand_9_out);
  not not_4 (not_4_out, counter_1_q[0]);
  LED led_5 (.in(not_2_out));
  LED led_6 (.in(not_1_out));
  LED led_7 (.in(not_3_out));
  LED led_8 (.in(not_3_out));
  LED led_9 (.in(not_4_out));
  LED led_10 (.in(not_1_out));
  LED led_11 (.in(not_2_out));

  // Notes on the sheet:
  //   B
  //   A
  //   C
  //   C
  //   D
  //   A
  //   B
endmodule
